# Fritzing sketch myLAB (saved by Fritzing 0.9.2b)

parts:
  Black_HAT1 = Black HAT Hack3r [form=male package=THT]
  Raspberry_Pi1 = Raspberry Pi 2  # not connected
  U1 = Explorer HAT Pro [part_number="Explorer HAT Pro" package=THT]
  U2 = Propeller HAT [part_number="Propeller HAT" package=THT]  # not connected
  Part1 = LED Matrix - Serial Interface - Red/Green/Blue  # not connected
  Black_HAT2 = Black HAT Hack3r [form=male package=THT]
  IC1 = Skywriter [chip_label=MGC3130 package=SMD]

nets:
  5V: Black_HAT1.pin2, U1.5v, Black_HAT2.5V
  N1: Black_HAT1.pin6, U1.Ground, Black_HAT2.GND
  N2: Black_HAT1.pin8, U1.RX
  N3: Black_HAT1.pin10, U1.TX
  N4: Black_HAT1.pin11, U1.CS
  N5: U1.MISO, Black_HAT2.GPIO10
  N6: U1.MOSI, Black_HAT2.GPIO9
  N7: U1.POW3V3, Black_HAT2.3V3
  N8: U1.PWM, Black_HAT2.GPIO18
  N9: U1.SCK, Black_HAT2.GPIO11
  N10: U1.SCL, Black_HAT2.GPIO3
  N11: U1.SDA, Black_HAT2.GPIO2
  N12: Black_HAT2.pin3, IC1.SDA
  N13: Black_HAT2.pin5, IC1.SCL
  N14: Black_HAT2.pin6, IC1.GND
  N15: Black_HAT2.pin17, IC1.VCC
  N16: Black_HAT2.pin19, IC1.RESET
  N17: Black_HAT2.pin21, IC1.TRFR

notes:
  Propeller HAT providing
  30 general purpose IO pins controllable by any of the
  8 cores of the Parallax Propeller microcontroller.
  GPIO8/CE0 on Explorer Pro is bridged to GPIO17 as reset for Propeller HAT.
  Use 'propman -p 8' when
  programming the HAT.
  Multiple GND+VCC avail.
  No other RPi GPIO though!
  Skywriter bridging #17/27 to MISO/MOSI for communication
  requires pull request #6
  commit 575a8ce
  UNI
  CORN
  HAT
  --------
  8x8
  RGB
  LEDs
  --------
  uses PWM only
  Explorer HAT Pro providing GPIO
  breakout for other HATs as well as its own functions: 8 Cap Touch pads,
  4 Analog inputs, 4 Digital inputs,
  4 Digital Outputs, 2 Motor drivers.

custom parts:
  Black HAT Hack3r: Raspberry Pi GPIO breakout and HAT debugging area
  Explorer HAT Pro: Explorer HAT Pro with 4 Output and 4 Input connections, 4 Analog Inputs and 2 bi-directional motor channels, plus power and ground.
  Skywriter: Electrical near-field 3D position data and gesture sensing.
